// Logisim project PRojecttttloggi.circ as structural Verilog
module main (
  input  P1,
  input  P2
);

  wire and_1_out, and_2_out, and_3_out, and_4_out, and_5_out, and_6_out, c_out, clock_1_out, combat_1_end1,
       combat_1_end2, combat_1_myd1, combat_1_myd2, d_ff_1_q, d_ff_2_q, d_ff_3_q, dipswitch_1_p2,
       dipswitch_2_p2, e0_out, led_decoder_1_l4, led_decoder_1_out_4, led_decoder_1_out_6,
       led_decoder_1_out_7, led_decoder_1_out_8, led_decoder_2_l4, led_decoder_2_out_4, led_decoder_2_out_6,
       led_decoder_2_out_7, led_decoder_2_out_8, my0_out, not_1_out, not_2_out, not_3_out, not_4_out,
       not_5_out, or_1_out, or_2_out, register_1_q, register_2_q, reset_out, state_1_q2, t_ff_1_q;
  wire [2:0] hp_minus1_1_out_3, hp_minus1_2_out_3;

  Button c (.out(c_out));
  Clock #(.highDuration(4), .lowDuration(4)) clock_1 (.out(clock_1_out));
  D_Flip_Flop d_ff_1 (.D(c_out), .clk(clock_1_out), .Q(d_ff_1_q));  // open: Qn, preset, reset
  D_Flip_Flop d_ff_2 (.D(d_ff_1_q), .clk(clock_1_out), .Q(d_ff_2_q));  // open: Qn, preset, reset
  // DipSwitch #(.number(1)) dipswitch_1: pin names not known; wires that end beside it: clock_1_out, dipswitch_1_p2, P1
  // DipSwitch #(.number(1)) dipswitch_2: pin names not known; wires that end beside it: P2, dipswitch_2_p2
  not not_1 (not_1_out, d_ff_2_q);
  Register #(.width(1)) register_1 (
    .D(dipswitch_1_p2), .en(and_1_out), .clk(clock_1_out), .Q(register_1_q));  // open: clr
  Register #(.width(1)) register_2 (
    .D(dipswitch_2_p2), .en(and_1_out), .clk(clock_1_out), .Q(register_2_q));  // open: clr
  and and_1 (and_1_out, d_ff_1_q, not_1_out);
  Button reset (.out(reset_out));
  LED_part led_1 (.in(and_1_out));
  T_Flip_Flop t_ff_1 (.T(d_ff_3_q), .clk(clock_1_out), .Q(t_ff_1_q), .reset(reset_out));  // open: Qn, preset
  not not_2 (not_2_out, hp_minus1_1_out_3[2]);
  combat combat_1 (
    .T(t_ff_1_q), .Xl(register_1_q), .Rl(register_2_q), .myd2(combat_1_myd2), .myd1(combat_1_myd1),
    .end2(combat_1_end2), .end1(combat_1_end1));
  // Probe on hp_minus1_1_out_3
  HP_Minus1 hp_minus1_1 (.hit(and_3_out), .init(reset_out), .out_3(hp_minus1_1_out_3));
  HP_Minus1 hp_minus1_2 (.hit(and_4_out), .init(reset_out), .out_3(hp_minus1_2_out_3));
  or or_1 (or_1_out, combat_1_myd2, combat_1_myd1);
  or or_2 (or_2_out, combat_1_end2, combat_1_end1);
  and and_2 (and_2_out, not_2_out, not_2_out);
  LED_part led_2 (.in(and_2_out));
  nor my0 (my0_out, hp_minus1_1_out_3[0], hp_minus1_1_out_3[1], hp_minus1_1_out_3[2]);
  nor e0 (e0_out, hp_minus1_2_out_3[0], hp_minus1_2_out_3[1], hp_minus1_2_out_3[2]);
  and and_3 (and_3_out, or_1_out, d_ff_3_q);
  and and_4 (and_4_out, d_ff_3_q, or_2_out);
  not not_3 (not_3_out, t_ff_1_q);
  LED_part Myturn (.in(not_3_out));
  LED_part EnTurn (.in(t_ff_1_q));
  LED_DECODER led_decoder_1 (
    .in_1(hp_minus1_1_out_3[2]), .Q1(hp_minus1_1_out_3[1]), .Q0(hp_minus1_1_out_3[0]),
    .out_4(led_decoder_1_out_4), .L4(led_decoder_1_l4), .out_6(led_decoder_1_out_6),
    .out_7(led_decoder_1_out_7), .out_8(led_decoder_1_out_8));
  LedBar #(.matrixcols(5)) Pl1 (
    .led0(led_decoder_1_out_4), .led1(led_decoder_1_l4), .led2(led_decoder_1_out_6),
    .led3(led_decoder_1_out_7), .led4(led_decoder_1_out_8));
  not not_4 (not_4_out, hp_minus1_2_out_3[2]);
  state state_1 (.mz(my0_out), .ez(e0_out), .T(t_ff_1_q), .Q2(state_1_q2));  // open: Q1, Q0
  and and_5 (and_5_out, not_4_out, not_4_out);
  LED_part led_3 (.in(and_5_out));
  not not_5 (not_5_out, state_1_q2);
  and and_6 (and_6_out, not_5_out, and_1_out);
  LedBar #(.matrixcols(5)) PL2 (
    .led0(led_decoder_2_out_4), .led1(led_decoder_2_l4), .led2(led_decoder_2_out_6),
    .led3(led_decoder_2_out_7), .led4(led_decoder_2_out_8));
  LED_DECODER led_decoder_2 (
    .in_1(hp_minus1_2_out_3[2]), .Q1(hp_minus1_2_out_3[1]), .Q0(hp_minus1_2_out_3[0]),
    .out_4(led_decoder_2_out_4), .L4(led_decoder_2_l4), .out_6(led_decoder_2_out_6),
    .out_7(led_decoder_2_out_7), .out_8(led_decoder_2_out_8));
  D_Flip_Flop d_ff_3 (.D(and_6_out), .clk(clock_1_out), .Q(d_ff_3_q));  // open: Qn, preset, reset

  // Notes on the sheet:
  //   0 atk/ 1 heavy atk
  //   0 def / 1 counter
endmodule

module HP_Minus1 (
  input  hit,
  input  init,
  output [2:0] out_3
);

  wire and_1_out, and_2_out, and_3_out, and_4_out, and_5_out, and_6_out, clock_1_out, not_1_out, not_2_out;
  wire [2:0] multiplexer_1_out, multiplexer_2_out, or_1_out;

  Multiplexer #(.width(3)) multiplexer_1 (.in0(multiplexer_2_out), .in1(3'b101), .out(multiplexer_1_out), .sel(init));
  Clock clock_1 (.out(clock_1_out));
  Register #(.width(3)) register_1 (.D(multiplexer_1_out), .clk(clock_1_out), .Q(out_3));  // open: en, clr
  // Probe on out_3
  not not_1 (not_1_out, out_3[1]);
  not not_2 (not_2_out, out_3[0]);
  Multiplexer #(.width(3)) multiplexer_2 (.in0(out_3), .in1(or_1_out), .out(multiplexer_2_out), .sel(hit));
  and and_1 (and_1_out, out_3[1], not_2_out);
  and and_2 (and_2_out, out_3[2], not_2_out);
  and and_3 (and_3_out, out_3[1], out_3[0]);
  and and_4 (and_4_out, out_3[2], not_1_out, not_2_out);
  and and_5 (and_5_out, out_3[2], out_3[0]);
  and and_6 (and_6_out, out_3[2], out_3[1]);
  or or_1 (or_1_out[0], and_1_out, and_2_out);
  or or_2 (or_1_out[1], and_3_out, and_4_out);
  or or_3 (or_1_out[2], and_5_out, and_6_out);
endmodule

module combat (
  input  T,
  input  Xl,
  input  Rl,
  output myd2,
  output myd1,
  output end2,
  output end1
);

  wire and_2_out, and_3_out, and_4_out, and_5_out, not_1_out, not_2_out, not_3_out;

  not not_1 (not_1_out, T);
  not not_2 (not_2_out, Xl);
  not not_3 (not_3_out, Rl);
  and and_1 (myd2, T, not_2_out, Rl);
  and and_2 (and_2_out, not_1_out, Xl, Rl);
  and and_3 (and_3_out, T, Xl, not_3_out);
  and and_4 (and_4_out, not_1_out, Xl, not_3_out);
  and and_5 (and_5_out, T, Xl, Rl);
  and and_6 (end1, not_1_out, not_2_out, Rl);
  or or_1 (myd1, and_2_out, and_3_out);
  or or_2 (end2, and_4_out, and_5_out);
endmodule

module state (
  input  mz,
  input  ez,
  input  T,
  output Q2,
  output Q1,
  output Q0
);

  wire and_1_out, and_2_out, and_3_out, not_1_out;

  not not_1 (not_1_out, ez);
  and and_1 (and_1_out, ez, T);
  and and_2 (and_2_out, not_1_out, T);
  and and_3 (and_3_out, mz, not_1_out);
  or or_1 (Q2, and_1_out, mz);
  or or_2 (Q0, and_2_out, and_3_out);

  assign Q1 = 1'b0;
endmodule

module LED_DECODER (
  input  in_1,
  input  Q1,
  input  Q0,
  output out_4,
  output L4,
  output out_6,
  output out_7,
  output out_8
);

  wire and_1_out, and_2_out, and_3_out;

  and and_1 (and_1_out, in_1, Q0);
  and and_2 (and_2_out, in_1, Q1);
  and and_3 (and_3_out, Q1, Q0);
  or or_1 (out_7, Q1, in_1);
  or or_2 (out_8, Q0, Q1, in_1);
  or or_3 (out_4, and_1_out, and_2_out);
  or or_4 (out_6, and_3_out, in_1);

  assign L4 = in_1;
endmodule

module LED (
  input  Q2,
  input  Q1,
  input  Q0,
  output L5,
  output L4,
  output L3,
  output L2,
  output L1
);

  wire and_1_out, and_2_out, and_3_out;

  and and_1 (and_1_out, Q2, Q0);
  and and_2 (and_2_out, Q2, Q1);
  and and_3 (and_3_out, Q1, Q0);
  or or_1 (L2, Q1, Q2);
  or or_2 (L1, Q0, Q1, Q2);
  or or_3 (L5, and_1_out, and_2_out);
  or or_4 (L3, and_3_out, Q2);

  assign L4 = Q2;
endmodule
